// Logisim project Team36.circ as structural Verilog: 2 circuits, main circuit main
module main (
);

  wire and_6_out, and_9_out, and_10_out, and_11_out, and_12_out, and_13_out, and_17_out, C0, C1, C2, CLK, D0,
       D1, D2, D3, D3T3, D4, D5, D6, D6T5, d_ff_1_q, DR_ZERO, INC_AC, INC_DR, INC_PC, INC_PC_t, LD_AC, LD_AR,
       LD_DR, LD_PC, or_2_out, or_3_out, or_4_out, or_6_out, or_7_out, or_9_out, or_12_out, READ, SC_CLR, T0,
       T1, T2, T3, T4, T5, T6, WRITE;
  wire [2:0] S0S1S2;
  wire [3:0] counter_1_q;
  wire [7:0] ADDRESS, AR_q, bit_extender_1_out, bit_extender_2_out, PC_q;
  wire [15:0] AC_OUT, alu_1_output, bit_extender_3_out, bit_extender_4_out, bit_extender_5_out, BUS_OUT,
       DR_OUT, IR_OUT, MEM_OUT, TR_OUT;

  Clock u_clk (.out(CLK));
  Counter #(.width(4), .max('hf)) counter_1 (
    .load(1'b0), .count(1'b1), .Q(counter_1_q), .clk(CLK), .clr(d_ff_1_q));  // open: D, carry
  D_Flip_Flop d_ff_1 (.clk(CLK), .D(SC_CLR), .Q(d_ff_1_q));  // open: Qn, preset, en, reset
  and and_1 (LD_PC, D4, T3);
  or or_1 (READ, LD_DR, T1);
  or or_2 (or_2_out, D0, D1, D5);
  or or_3 (or_3_out, D0, D2);
  or or_4 (or_4_out, D0, D5);
  and and_2 (C1, or_3_out, T4);
  and and_3 (C2, or_4_out, T4);
  Bit_Extender #(.in_width(16), .out_width(8)) bit_extender_1 (.in(BUS_OUT), .out(bit_extender_1_out));
  Bit_Extender #(.in_width(16), .out_width(8)) bit_extender_2 (.in(BUS_OUT), .out(bit_extender_2_out));
  Decoder #(.select(4), .enable("false")) decoder_1 (
    .out0(T0), .out1(T1), .out2(T2), .out3(T3), .out4(T4), .out5(T5), .out6(T6), .sel(counter_1_q));  // open: out7, out8, out9, out10, out11, out12, out13, out14, out15
  and and_4 (C0, or_2_out, T4);
  ALU alu_1 (.DR(DR_OUT), .AC(AC_OUT), .C2C1C0({C2, C1, C0}), .Output(alu_1_output));
  Decoder #(.select(3), .disabled(0), .enable("false")) decoder_2 (
    .out0(D0), .out1(D2), .out2(D1), .out3(D3), .out4(D4), .out5(D5), .out6(D6), .sel(IR_OUT[14:12]));  // open: out7
  Counter AR (.load(LD_AR), .D(bit_extender_1_out), .count(1'b0), .Q(AR_q), .clk(CLK), .clr(1'b0));  // open: carry
  Counter PC (.load(LD_PC), .D(bit_extender_2_out), .count(INC_PC), .Q(PC_q), .clk(CLK), .clr(1'b0));  // open: carry
  Counter #(.width(16), .max('hffff)) DR (
    .load(LD_DR), .D(BUS_OUT), .count(INC_DR), .Q(DR_OUT), .clk(CLK), .clr(1'b0));  // open: carry
  Counter #(.width(16), .max('hffff)) AC (
    .load(LD_AC), .D(alu_1_output), .count(1'b0), .Q(AC_OUT), .clk(CLK), .clr(1'b0));  // open: carry
  Register #(.width(16)) IR (.D(BUS_OUT), .en(T1), .Q({IR_OUT[15:12], ADDRESS, IR_OUT[3:0]}), .clk(CLK), .clr(1'b0));
  Counter #(.width(16), .max('hffff)) TR (
    .load(1'b0), .D(BUS_OUT), .count(1'b0), .Q(TR_OUT), .clk(CLK), .clr(1'b0));  // open: carry
  and and_5 (D3T3, D3, T3);
  and and_6 (and_6_out, D6, T5);
  RAM #(.dataWidth(16), .bus("separate")) ram_1 (
    .addr(AR_q), .din(BUS_OUT), .data(MEM_OUT), .str(WRITE), .clk(CLK), .ld(READ));  // open: sel, clr
  assign bit_extender_3_out = {{8{1'b0}}, AR_q};  // Bit_Extender bit_extender_3
  assign bit_extender_4_out = {{8{1'b0}}, PC_q};  // Bit_Extender bit_extender_4
  or or_5 (WRITE, D3T3, and_6_out);
  and and_7 (INC_AC, D5, T4);
  assign bit_extender_5_out = {{8{1'b0}}, ADDRESS};  // Bit_Extender bit_extender_5
  Multiplexer #(.select(3), .width(16), .enable("false")) multiplexer_1 (
    .in1(MEM_OUT), .in2(bit_extender_3_out), .in3(bit_extender_4_out), .in4(DR_OUT), .in5(AC_OUT),
    .in6(bit_extender_5_out), .in7(TR_OUT), .out(BUS_OUT), .sel(S0S1S2));  // open: in0
  and and_8 (D6T5, D6, T5);
  and and_9 (and_9_out, D3, T3);
  and and_10 (and_10_out, D4, T3);
  or or_6 (or_6_out, D0, D1, D2, D5);
  and and_11 (and_11_out, D6, T5);
  and and_12 (and_12_out, DR_ZERO, D6T5);
  and and_13 (and_13_out, T4, or_6_out);
  or or_7 (or_7_out, D0, D1, D2, D5, D6);
  or or_8 (INC_PC_t, and_12_out, T1);
  or or_9 (or_9_out, D0, D1, D2, D5);
  or or_10 (LD_AR, T0, T2);
  or or_11 (SC_CLR, and_9_out, and_10_out, and_13_out, and_11_out);
  and and_14 (LD_DR, or_7_out, T3);
  and and_15 (INC_DR, D6, T4);
  and and_16 (LD_AC, or_9_out, T4);
  Comparator #(.width(16)) comparator_1 (.a(DR_OUT), .b({16{1'b0}}), .eq(DR_ZERO));  // open: gt, lt
  and and_17 (and_17_out, D1, T4);
  or or_12 (or_12_out, and_17_out, D6T5);
  Priority_Encoder priority_encoder_1 (
    .in1(READ), .in2(LD_PC), .in3(T0), .in4(or_12_out), .in5(D3T3), .in6(T2), .out(S0S1S2));  // open: in0, in7, en_in, gs, en_out

  // Other names for the same wires on the sheet: IR_OUT[11:4] = ADDRESS; T3D01256 = LD_DR
endmodule

module ALU (
  input  [15:0] DR,
  input  [15:0] AC,
  input  [2:0] C2C1C0,
  output [15:0] Output
);

  wire [15:0] adder_1_out, divider_1_out, multiplier_1_out, not_1_out, subtractor_1_out, xor_1_out;

  Divider #(.width(16)) divider_1 (.a(AC), .b(DR), .out(divider_1_out));  // open: upper, rem
  Adder #(.width(16)) adder_1 (.a(DR), .b(AC), .out(adder_1_out));  // open: cin, cout
  Subtractor #(.width(16)) subtractor_1 (.a(DR), .b(AC), .out(subtractor_1_out));  // open: bin, bout
  Multiplier #(.width(16)) multiplier_1 (.a(DR), .b(AC), .out(multiplier_1_out));  // open: cin, cout
  assign not_1_out = ~DR;  // NOT_Gate not_1, 16 bits wide
  assign xor_1_out = DR ^ AC;  // XOR_Gate xor_1, 16 bits wide
  Multiplexer #(.select(3), .width(16), .enable("false")) multiplexer_1 (
    .in1(DR), .in2(adder_1_out), .in3(subtractor_1_out), .in4(multiplier_1_out), .in5(divider_1_out),
    .in6(not_1_out), .in7(xor_1_out), .out(Output), .sel(C2C1C0));  // open: in0
endmodule
